# Fritzing sketch HardcodedDispenser (saved by Fritzing 1.0.3b)
circuit board: 8.46667cm x 5.64444cm
breadboards: 1

parts:
  J1 = Basic Servo
  J2 = Basic Servo
  LED1 = LED - 5mm [color="Blue (470nm)" current=0.030A package="5 mm [THT]"]
  R1 = Resistor [tolerance=±5% power=0.25W resistance=220 package=THT]
  C1 = Electrolytic Capacitor [capacitance=100µF voltage=16V package="100 mil [THT, electrolytic]"]
  C2 = Electrolytic Capacitor [capacitance=100µF voltage=16V package="100 mil [THT, electrolytic]"]
  S1 = Pushbutton [package="[THT]"]
  R2 = Resistor [tolerance=±5% power=0.25W resistance=10k package=THT]
  DRV_1 = DRV 8825 Stepper Motor Carrier, High Current [part_number="DRV 8825"]
  M1 = Stepper Motor - Bipolar
  Part1 = Arduino Nano (Rev3.0)
  C3 = Electrolytic Capacitor [capacitance=100µF voltage=16V package="100 mil [THT, electrolytic]"]
  J3 = Screw terminal - 2 pins [package=THT]
  JP1 = Header 4 [package=jst-4-pth]
  M2 = RioRand LM2596
  M3 = RioRand LM2596
  M4 = fc-51 [package=THT]
  C4 = Ceramic Capacitor [capacitance=0.1µF voltage=35V package="100 mil [THT, multilayer]"]

nets:
  GND: J1.gnd, J2.gnd, LED1.cathode, C1.-, C2.-, R2.Pin_1, DRV_1.GROUND_ST/_MT, DRV_1.GROUND_LOG, Part1.GND, C3.-, J3.pin2, M2.Pin_2, M2.Pin_4, M3.Pin_2, M3.Pin_4
  VCC: J1.vcc, J2.vcc, C1.+, C2.+, M2.Pin_3
  N1: J1.pulse, Part1.D5
  N2: J2.pulse, Part1.D6
  N3: LED1.anode, R1.Pin_0
  N4: R1.Pin_1, Part1.D9
  N5: S1.Pin_1, S1.Pin_2, R2.Pin_0, DRV_1.VOLTAGE_DD, Part1.5V
  N6: S1.Pin_4, Part1.D3
  N7: DRV_1.RESET, DRV_1.SLEEP
  N8: DRV_1.STEP, Part1.A2
  N9: DRV_1.DIRECTION, Part1.A1
  N10: DRV_1.VOLTAGE_ST/_MT, C3.+, J3.pin1, M2.Pin_1, M3.Pin_1
  N11: DRV_1.OUT_2B, M1.A
  N12: DRV_1.OUT_2A, M1.C
  N13: DRV_1.OUT_1A, M1.B
  N14: DRV_1.OUT_1B, M1.D
  N15: Part1.D4, M4.pin1
  N16: Part1.D10, JP1.4
  N17: Part1.D11/MOSI, JP1.3
  N18: Part1.D12/MISO, JP1.2
  N19: Part1.VIN, M3.Pin_3
  N20: Part1.D13/SCK, JP1.1
  N21: M4.pin2, C4.0
  N22: M4.pin3, C4.1

notes:
  SPI Connection
  12V
  12V -> 7V
  12V -> 5V
  Hardcoded Dispensing Unit
